# Fritzing sketch yapay kalp devresi v1.0 (saved by Fritzing 0.9.3b)
breadboards: 1

parts:
  M1 = DC Motor
  J1 = Basic Servo
  J2 = Basic Servo
  Parça1 = Arduino Nano (Rev3.0) (ICSP)

nets:
  N1: M1.pin_1, Parça1.D7
  GND: M1.pin_2, J1.gnd, J2.gnd, Parça1.GND
  VCC: J1.vcc, J2.vcc, Parça1.5V
  N2: J1.pulse, Parça1.D5
  N3: J2.pulse, Parça1.D4

notes:
  SU MOTORU/SU POMPASI
